# Fritzing sketch droppboll_koppling (saved by Fritzing 0.9.2b)
breadboards: 1

parts:
  L1 = Solenoid
  IR2 = TSOP312.., 314.. [package=THT]
  P2 = S1133 Si Photodiode [package="8mm Ceramic [THT]"]  # not connected
  Q1 = Basic FET P-Channel [package="TO220 [THT]"]
  Q2 = Basic FET P-Channel [package="DPak [SMD]"]
  D1 = Diode [package=diode-hv]
  R1 = Resistor [tolerance=±5% resistance=220 package=THT]
  Part2 = Arduino Uno (Rev3)
  R2 = Resistor [tolerance=±5% resistance=220 package=THT]
  D2 = Diode [package=diode-hv]
  L2 = Solenoid
  IR3 = TSOP312.., 314.. [package=THT]
  P3 = S1133 Si Photodiode [package="8mm Ceramic [THT]"]

nets:
  N1: L1.pin1, Q2.drain, D2.A
  N2: L1.pin2, D1.C, Part2.5V, D2.C, L2.pin2, IR3.Vs, P3.anode
  N3: IR2.Data, Part2.D4
  N4: Q1.gate, R1.Pin_0
  N5: Q1.drain, D1.A, L2.pin1
  GND: Q1.source, Q2.source, Part2.GND, IR3.GND, P3.cathode
  N6: Q2.Gate, R2.Pin_0
  N7: R1.Pin_1, Part2.D7
  N8: Part2.D5_PWM, IR3.Data
  N9: Part2.D6_PWM, R2.Pin_1

notes:
  SOLENOID 1
  SOLENOID 2
  IR SENSOR 1
  IR SENSOR 2
